// Logisim project Lab6.circ as structural Verilog: 1 circuit, main circuit main
module main (
  input  [1:0] Access_Mem,
  input  [31:0] Mem_Address,
  input  [31:0] Mem_Write,
  input  Mem_Write_Enable
);

  wire clock_1_out, not_1_out, not_2_out;
  wire [31:0] ram_1_dout;

  Clock clock_1 (.out(clock_1_out));
  // NAND_Gate byte has open pins: in0=Access_Mem[0], in1=Access_Mem[1], out=open
  not not_1 (not_1_out, Access_Mem[0]);
  // AND_Gate halfword has open pins: in0=not_1_out, in1=Access_Mem[1], out=open
  not not_2 (not_2_out, Access_Mem[1]);
  // AND_Gate word has open pins: in0=Access_Mem[0], in1=not_2_out, out=open
  RAM #(.addrWidth(24), .byteenables("byteEnables"), .dataWidth(32)) ram_1 (
    .addr(Mem_Address[31:8]), .we(Mem_Write_Enable), .oe(1'b1), .clk(clock_1_out), .din(Mem_Write),
    .dout(ram_1_dout));  // open: be3, be2, be1, be0
endmodule
